// Logisim project CPU16BIT.circ as structural Verilog
// COMPUTER
module FINAL_BUILD (
  input  in_1,
  input  clk_enb
);

  wire A_AND_B, A_NAND_B, A_NOR_B, A_OR_B, A_XOR_B, ACC_READ, ACC_WRITE, ADD, ADDRESS_WRITE,
       alu_1_borrow_out, alu_1_carry_out, alu_1_equals, alu_1_greater, alu_1_less, alu_1_zero, button_1_out,
       button_2_out, clock_1_out, clock_2_out, CMP, CTN_ENB, CTN_OUT, DATA_WRITE, decoder_1_out6, DIS_READ,
       DIS_WRITE, HALT, INSTRUCT_READ, INSTRUCT_WRITE, JUMP, KB_REG_LOAD, KB_REG_OUT, MAR_READ, MAR_WRITE,
       not_1_out, not_2_out, NOT_A, or_1_out, or_2_out, or_3_out, or_4_out, Pulse, RAM_IN, RAM_OUT, READ_B,
       READ_X, READ_Y, RESET, reset_flag, STACK_DATA_OUT, STACK_DOWN, STACK_STORE, STACK_UP, SUB, TTY_WRITE,
       UPDATE_DISPLAY, UPPER_BITS, WRITE_B, WRITE_X, WRITE_Y;
  wire [2:0] ADDRESS_IN;
  wire [3:3] step_counter_1_binary_out;
  wire [6:0] keyboard_1_data;
  wire [7:0] counter_1_q, video_buffer_1_line_1, video_buffer_1_line_2, video_buffer_1_line_3,
       video_buffer_1_line_4, video_buffer_1_line_5, video_buffer_1_line_6, video_buffer_1_line_7,
       video_buffer_1_line_8;
  wire [7:3] DATA_IN;
  wire [14:6] rom_3_data;
  wire [15:0] acculumator_1_always_out, ADDRESS, b_register_1_always_out, instruction_register_1_always_out,
       memory_address_register_1_always_out, ram_1_dout, ram_2_dout;
  wire [15:8] DATA_IN_OUT, instruction_register_1_data_out;

  ROM #(.addrWidth(16), .dataWidth(16)) rom_1 (
    .addr(ADDRESS),
    .data({STACK_DATA_OUT, UPPER_BITS, ACC_READ, CMP, SUB, ADD, STACK_UP, KB_REG_OUT, READ_B, READ_Y, READ_X, INSTRUCT_READ, MAR_READ, CTN_ENB, RAM_OUT, CTN_OUT}));
  or or_1 (or_1_out, RESET, decoder_1_out6);
  or or_2 (or_2_out, STACK_DOWN, STACK_UP);
  LED led_1 (.in(step_counter_1_binary_out[3]));
  not not_1 (not_1_out, Pulse);
  Button button_1 (.out(button_1_out));
  not not_2 (not_2_out, STACK_DOWN);
  LED led_2 (.in(ADDRESS[2]));
  LED led_3 (.in(ADDRESS[1]));
  LED led_4 (.in(ADDRESS[0]));
  STEP_COUNTER step_counter_1 (
    .RESET(or_1_out), .CLOCK(not_1_out), .BINARY_OUT({step_counter_1_binary_out[3], ADDRESS[2:0]}));
  Counter counter_1 (
    .clr(button_1_out), .up(not_2_out), .count(or_2_out), .clk(or_2_out), .Q(counter_1_q));  // open: load, D, carry
  Decoder #(.enable("false"), .select(4)) decoder_1 (
    .out6(decoder_1_out6), .sel({step_counter_1_binary_out[3], ADDRESS[2:0]}));  // open: out0, out1, out2, out3, out4, out5, out7, out8, out9, out10, out11, out12, out13, out14, out15
  ROM #(.addrWidth(16), .dataWidth(16)) rom_2 (
    .addr(ADDRESS),
    .data({UPDATE_DISPLAY, DATA_WRITE, JUMP, STACK_DOWN, STACK_STORE, RAM_IN, KB_REG_LOAD, TTY_WRITE, ADDRESS_WRITE, WRITE_Y, WRITE_X, reset_flag, WRITE_B, ACC_WRITE, INSTRUCT_WRITE, MAR_WRITE}));
  MEMORY_ADDRESS_REGISTER memory_address_register_1 (
    .DATA_IN({DATA_IN_OUT, DATA_IN, ADDRESS_IN}), .MAR_IN(MAR_WRITE), .MAR_OUT(MAR_READ), .CLOCK(Pulse),
    .MAR_RESET(RESET), .ALWAYS_OUT(memory_address_register_1_always_out),
    .DATA_OUT({DATA_IN_OUT, DATA_IN, ADDRESS_IN}));
  RAM #(.addrWidth(16), .dataWidth(16), .enables("line")) ram_1 (
    .addr(memory_address_register_1_always_out), .we(RAM_IN), .clk(clock_1_out),
    .din({DATA_IN_OUT, DATA_IN, ADDRESS_IN}), .dout(ram_1_dout));
  Clock clock_1 (.out(clock_1_out));
  PROGRAM_COUNTER program_counter_1 (
    .COUNTER_OUT(CTN_OUT), .RESET(RESET), .JUMP(JUMP), .COUNTER_ENABLE(CTN_ENB), .CLOCK(Pulse),
    .ADDRESS_IN({DATA_IN_OUT, DATA_IN, ADDRESS_IN}), .ADDRESS_OUT({DATA_IN_OUT, DATA_IN, ADDRESS_IN}));  // open: ALWAYS_OUT
  RAM #(.dataWidth(16), .enables("line")) ram_2 (
    .addr(counter_1_q), .we(STACK_STORE), .clk(Pulse), .din({DATA_IN_OUT, DATA_IN, ADDRESS_IN}),
    .dout(ram_2_dout));
  INSTRUCTION_REGISTER instruction_register_1 (
    .STORE(INSTRUCT_WRITE), .DATA_OUT_ENABLE(INSTRUCT_READ), .RESET(RESET), .CLOCK(Pulse),
    .DATA_IN({DATA_IN_OUT, DATA_IN, ADDRESS_IN}),
    .ALWAYS_OUT({instruction_register_1_always_out[15], ADDRESS[9:3], instruction_register_1_always_out[7:0]}),
    .DATA_OUT({instruction_register_1_data_out, DATA_IN, ADDRESS_IN}));
  Pull_Resistor pull_resistor_1 (.node(ADDRESS[15]));
  assign {DATA_IN_OUT, DATA_IN, ADDRESS_IN} = RAM_OUT ? ram_1_dout : 16'bz;  // Controlled_Buffer controlled_buffer_1
  assign DATA_IN_OUT = UPPER_BITS ? instruction_register_1_always_out[7:0] : 8'bz;  // Controlled_Buffer controlled_buffer_2
  assign {DATA_IN_OUT, DATA_IN, ADDRESS_IN} = STACK_DATA_OUT ? ram_2_dout : 16'bz;  // Controlled_Buffer controlled_buffer_3
  ROM #(.addrWidth(16), .dataWidth(16)) rom_3 (
    .addr(ADDRESS), .data({HALT, rom_3_data, A_NOR_B, A_NAND_B, A_XOR_B, A_OR_B, A_AND_B, NOT_A}));
  Pull_Resistor pull_resistor_2 (.node(DATA_IN_OUT[15]));
  Pull_Resistor pull_resistor_3 (.node(DATA_IN_OUT[14]));
  Pull_Resistor pull_resistor_4 (.node(DATA_IN_OUT[13]));
  Pull_Resistor pull_resistor_5 (.node(DATA_IN_OUT[12]));
  Y_AND_Y_REGISTERS y_and_y_registers_1 (
    .WRITE_X(WRITE_X), .WRITE_Y(WRITE_Y), .READ_X(READ_X), .READ_Y(READ_Y), .CLOCK(Pulse), .RESET(RESET),
    .in_1({DATA_IN_OUT, DATA_IN, ADDRESS_IN}), .DATA_OUT({DATA_IN_OUT, DATA_IN, ADDRESS_IN}));  // open: X_ALWAYS_OUT, Y_ALWAYS_OUT
  Pull_Resistor pull_resistor_6 (.node(DATA_IN_OUT[11]));
  Pull_Resistor pull_resistor_7 (.node(DATA_IN_OUT[10]));
  Pull_Resistor pull_resistor_8 (.node(DATA_IN_OUT[9]));
  Pull_Resistor pull_resistor_9 (.node(DATA_IN_OUT[8]));
  Pull_Resistor pull_resistor_10 (.node(DATA_IN[7]));
  Pull_Resistor pull_resistor_11 (.node(DATA_IN[6]));
  Pull_Resistor pull_resistor_12 (.node(DATA_IN[5]));
  Pull_Resistor pull_resistor_13 (.node(DATA_IN[4]));
  Pull_Resistor pull_resistor_14 (.node(DATA_IN[3]));
  Pull_Resistor pull_resistor_15 (.node(ADDRESS_IN[2]));
  Pull_Resistor pull_resistor_16 (.node(ADDRESS_IN[1]));
  Pull_Resistor pull_resistor_17 (.node(ADDRESS_IN[0]));
  assign {DATA_IN[6:3], ADDRESS_IN} = KB_REG_OUT ? keyboard_1_data : 7'bz;  // Controlled_Buffer controlled_buffer_4
  Button button_2 (.out(button_2_out));
  OUTPUT_REGISTER output_register_1 (
    .OUTPUT_WRITE(DIS_WRITE), .OUTPUT_READ(DIS_READ), .CLOCK(Pulse), .RESET(RESET),
    .DATA_IN({DATA_IN_OUT, DATA_IN, ADDRESS_IN}), .DATA_OUT({DATA_IN_OUT, DATA_IN, ADDRESS_IN}));  // open: ALWAYS_OUT
  TTY #(.rows(12)) tty_1 (.data({DATA_IN[6:3], ADDRESS_IN}), .clk(Pulse), .we(TTY_WRITE), .clr(RESET));
  Clock clock_2 (.out(clock_2_out));
  CLK clk_1 (
    .CLOCK_IN(clock_2_out), .CLOCK_ENABLE(clk_enb), .MANUAL_TICK(button_2_out), .HALT(HALT), .CLOCK_OUT(Pulse));
  ACCULUMATOR acculumator_1 (
    .A_WRITE(ACC_WRITE), .A_READ(ACC_READ), .CLOCK(Pulse), .RESET(RESET),
    .DATA_IN({DATA_IN_OUT, DATA_IN, ADDRESS_IN}), .ALWAYS_OUT(acculumator_1_always_out),
    .DATA_OUT({DATA_IN_OUT, DATA_IN, ADDRESS_IN}));
  B_REGISTER b_register_1 (
    .B_WRITE(WRITE_B), .B_READ(READ_B), .CLOCK(Pulse), .RESET(RESET),
    .DATA_IN({DATA_IN_OUT, DATA_IN, ADDRESS_IN}), .ALWAYS_OUT(b_register_1_always_out),
    .DATA_OUT({DATA_IN_OUT, DATA_IN, ADDRESS_IN}));
  Button button_3 (.out(RESET));
  Keyboard keyboard_1 (.clk(KB_REG_LOAD), .data(keyboard_1_data));  // open: re, clr, avail
  DotMatrix #(.inputtype("row"), .matrixcols(8), .matrixrows(8)) dotmatrix_1 (
    .row0(video_buffer_1_line_1), .row1(video_buffer_1_line_2), .row2(video_buffer_1_line_3),
    .row3(video_buffer_1_line_4), .row4(video_buffer_1_line_5), .row5(video_buffer_1_line_6),
    .row6(video_buffer_1_line_7), .row7(video_buffer_1_line_8));
  video_buffer video_buffer_1 (
    .DATA_WRITE_ENABLE(DATA_WRITE), .CLOCK(Pulse), .UPDATE_DISPLAY(UPDATE_DISPLAY),
    .DATA_IN({DATA_IN, ADDRESS_IN}), .RESET_DISPLAY(in_1), .RESET_BUFFER(in_1), .ADDRESS_SELECT(ADDRESS_IN),
    .BUFFER_ADDRESS_WRITE_ENB(ADDRESS_WRITE), .LINE_1(video_buffer_1_line_1), .LINE_2(video_buffer_1_line_2),
    .LINE_3(video_buffer_1_line_3), .LINE_4(video_buffer_1_line_4), .LINE_5(video_buffer_1_line_5),
    .LINE_6(video_buffer_1_line_6), .LINE_7(video_buffer_1_line_7), .LINE_8(video_buffer_1_line_8));
  ALU alu_1 (
    .ADD(ADD), .SUB(SUB), .NOT_A(NOT_A), .A_AND_B(A_AND_B), .A_OR_B(A_OR_B), .A_XOR_B(A_XOR_B),
    .A_NAND_B(A_NAND_B), .A_NOR_B(A_NOR_B), .A_IN(acculumator_1_always_out), .B_IN(b_register_1_always_out),
    .ZERO(alu_1_zero), .DATA_OUT({DATA_IN_OUT, DATA_IN, ADDRESS_IN}), .CARRY_OUT(alu_1_carry_out),
    .BORROW_OUT(alu_1_borrow_out), .GREATER(alu_1_greater), .EQUALS(alu_1_equals), .LESS(alu_1_less));  // open: BORROW_IN, CARRY_IN
  or or_3 (or_3_out, SUB, ADD);
  FLAGS flags_1 (
    .ALU_FLAGS_SET(or_3_out), .COMPARE_FALGS_SET(CMP), .CLOCK(Pulse), .RESET(or_4_out),
    .CARRY(alu_1_carry_out), .BORROW(alu_1_borrow_out), .GREATER(alu_1_greater), .EQUALS(alu_1_equals),
    .LESS(alu_1_less), .ZERO(alu_1_zero), .ZERO_FLAG(ADDRESS[11]), .CARRY_FLAG(ADDRESS[14]),
    .GREATER_FLAG(ADDRESS[13]), .EQUALS_FLAG(ADDRESS[12]), .LESS_FLAG(ADDRESS[10]));  // open: BORROW_FLAG
  or or_4 (or_4_out, reset_flag, RESET);

  // Other names for the same wires on the sheet: LESS_FLAG = ADDRESS[10]; ZERO_FLAG = ADDRESS[11];
  //   EQUALS_FLAG = ADDRESS[12]; GREATER_FLAG = ADDRESS[13]; CARRY_FLAG = ADDRESS[14]; DATA_IN[2:0] = ADDRESS_IN;
  //   DATA_IN_OUT[7:0] = {DATA_IN, ADDRESS_IN}; TTY_OUT[6:0] = {DATA_IN[6:3], ADDRESS_IN}

  // Notes on the sheet:
  //   contents of rom_1 (hex, n*v repeats v):
  //   1 6 6*0 1 6 10 2 4*0 1 6 10 2 4*0 1 6 10 2 4*0 1 6 10 2 4*0 1 6 10 2 4*0 1 6 10 5*0 1 6 10 1 4*0 1 6
  //   10 5*0 1 6 10 5*0 1 6 10 5*0 1 6 10 2000 4*0 1 6 10 80 4*0 1 6 10 20 4*0 1 6 10 40 4*0 1 6 10 100
  //   4*0 1 6 10 2 400 0 0 0 1 6 10 2 800 0 0 0 1 6 10 2 1000 0 0 0 1 6 10 400 4*0 1 6 10 800 4*0 1 6 6*0
  //   1 6 6*0 1 6 6*0 1 6 6*0 1 6 6*0 1 6 6*0 1 6 6*0 1 6 6*0 1 6 6*0 1 6 6*0 1 6 6*0 1 6 20 40 4*0 1 6 20
  //   2 4*0 1 6 40 5*0 1 6 6*0 1 6 6*0 1 6 6*0 1 6 6*0 1 6 6*0 1 6 6*0 1 6 6*0 1 6 6*0 1 6 6*0 1 6 6*0 1 6
  //   6*0 1 6 6*0 1 6 6*0 1 6 200 1 10 0 0 0 1 6 8000 5*0 1 6 200 1 4000 400 0 0 1 6 6*0 1 6 6*0 1 6 6*0 1
  //   6 6*0 1 6 6*0 1 6 6*0 1 6 6*0 1 6 6*0 1 6 6*0 1 6 6*0 1 6 6*0 1 6 6*0 1 6 6*0 1 6 10 5*0 1 6 10 5*0
  //   1 6 6*0 1 6 10 2 4*0 1 6 10 2 4*0 1 6 6*0 1 6 6*0 1 6 6*0 1 6 6*0 1 6 6*0 1 6 6*0 1 6 6*0 1 6 6*0 1
  //   6 6*0 1 6 6*0 1 6 6*0 1 6 10 5*0 1 6 10 2 4*0 1 6 10 2 4*0 1 6 10 2 4*0 1 6 6*0 1 6 6*0 1 6 6*0 1 6
  //   6*0 1 6 6*0 1 6 6*0 1 6 6*0 1 6 6*0 1 6 6*0 1 6 6*0 1 6 6*0 1 6 6*0 1 6 6*0 1 6 6*0 1 6 6*0 1 6 6*0
  //   1 6 6*0 1 6 6*0 1 6 6*0 1 6 6*0 1 6 6*0 1 6 6*0 1 6 6*0 1 6 6*0 1 6 6*0 1 6 6*0 1 6 6*0 1 6 6*0 1 6
  //   10 5*0 1 6 6*0 1 6 6*0 1 6 6*0 1 6 6*0 1 6 6*0 1 6 40 5*0 1 6 4000 400 2000 0 0 0 1 6 6*0 1 6 6*0 1
  //   6 6*0 1 6 6*0 1 6 6*0 1 6 6*0 1 6 6*0 1 6 6*0 1 6 6*0 1 6 10 2 4*0 1 6 10 2 4*0 1 6 10 2 4*0 1 6 10
  //   2 4*0 1 6 10 2 4*0 1 6 10 5*0 1 6 10 1 4*0 1 6 10 5*0 1 6 10 5*0 1 6 10 5*0 1 6 10 2000 4*0 1 6 10
  //   80 4*0 1 6 10 20 4*0 1 6 10 40 4*0 1 6 10 100 4*0 1 6 10 2 400 0 0 0 1 6 10 2 800 0 0 0 1 6 10 2
  //   1000 0 0 0 1 6 10 400 4*0 1 6 10 800 4*0 1 6 6*0 1 6 6*0 1 6 6*0 1 6 6*0 1 6 6*0 1 6 6*0 1 6 6*0 1 6
  //   6*0 1 6 6*0 1 6 6*0 1 6 6*0 1 6 20 40 4*0 1 6 20 2 4*0 1 6 40 5*0 1 6 6*0 1 6 6*0 1 6 6*0 1 6 6*0 1
  //   6 6*0 1 6 6*0 1 6 6*0 1 6 6*0 1 6 6*0 1 6 6*0 1 6 6*0 1 6 6*0 1 6 6*0 1 6 200 1 10 0 0 0 1 6 8000
  //   5*0 1 6 200 1 4000 400 0 0 1 6 6*0 1 6 6*0 1 6 6*0 1 6 6*0 1 6 6*0 1 6 6*0 1 6 6*0 1 6 6*0 1 6 6*0 1
  //   6 6*0 1 6 6*0 1 6 6*0 1 6 6*0 1 6 10 5*0 1 6 10 5*0 1 6 6*0 1 6 10 2 4*0 1 6 10 2 4*0 1 6 6*0 1 6
  //   6*0 1 6 6*0 1 6 6*0 1 6 6*0 1 6 6*0 1 6 6*0 1 6 6*0 1 6 6*0 1 6 6*0 1 6 6*0 1 6 10 5*0 1 6 10 2 4*0
  //   1 6 10 2 4*0 1 6 10 2 4*0 1 6 6*0 1 6 6*0 1 6 6*0 1 6 6*0 1 6 6*0 1 6 6*0 1 6 6*0 1 6 6*0 1 6 6*0 1
  //   6 6*0 1 6 6*0 1 6 6*0 1 6 6*0 1 6 6*0 1 6 6*0 1 6 6*0 1 6 6*0 1 6 6*0 1 6 6*0 1 6 6*0 1 6 6*0 1 6
  //   6*0 1 6 6*0 1 6 6*0 1 6 6*0 1 6 6*0 1 6 6*0 1 6 6*0 1 6 10 5*0 1 6 10 5*0 1 6 6*0 1 6 6*0 1 6 6*0 1
  //   6 6*0 1 6 40 5*0 1 6 4000 400 2000 0 0 0 1 6 6*0 1 6 6*0 1 6 6*0 1 6 6*0 1 6 6*0 1 6 6*0 1 6 6*0 1 6
  //   6*0 1 6 6*0 1 6 10 2 4*0 1 6 10 2 4*0 1 6 10 2 4*0 1 6 10 2 4*0 1 6 10 2 4*0 1 6 10 5*0 1 6 10 1 4*0
  //   1 6 10 5*0 1 6 10 5*0 1 6 10 5*0 1 6 10 2000 4*0 1 6 10 80 4*0 1 6 10 20 4*0 1 6 10 40 4*0 1 6 10
  //   100 4*0 1 6 10 2 400 0 0 0 1 6 10 2 800 0 0 0 1 6 10 2 1000 0 0 0 1 6 10 400 4*0 1 6 10 800 4*0 1 6
  //   6*0 1 6 6*0 1 6 6*0 1 6 6*0 1 6 6*0 1 6 6*0 1 6 6*0 1 6 6*0 1 6 6*0 1 6 6*0 1 6 6*0 1 6 20 40 4*0 1
  //   6 20 2 4*0 1 6 40 5*0 1 6 6*0 1 6 6*0 1 6 6*0 1 6 6*0 1 6 6*0 1 6 6*0 1 6 6*0 1 6 6*0 1 6 6*0 1 6
  //   6*0 1 6 6*0 1 6 6*0 1 6 6*0 1 6 200 1 10 0 0 0 1 6 8000 5*0 1 6 200 1 4000 400 0 0 1 6 6*0 1 6 6*0 1
  //   6 6*0 1 6 6*0 1 6 6*0 1 6 6*0 1 6 6*0 1 6 6*0 1 6 6*0 1 6 6*0 1 6 6*0 1 6 6*0 1 6 6*0 1 6 10 5*0 1 6
  //   10 5*0 1 6 6*0 1 6 10 2 4*0 1 6 10 2 4*0 1 6 6*0 1 6 6*0 1 6 6*0 1 6 6*0 1 6 6*0 1 6 6*0 1 6 6*0 1 6
  //   6*0 1 6 6*0 1 6 6*0 1 6 6*0 1 6 10 5*0 1 6 10 2 4*0 1 6 10 2 4*0 1 6 10 2 4*0 1 6 6*0 1 6 6*0 1 6
  //   6*0 1 6 6*0 1 6 6*0 1 6 6*0 1 6 6*0 1 6 6*0 1 6 6*0 1 6 6*0 1 6 6*0 1 6 6*0 1 6 6*0 1 6 6*0 1 6 6*0
  //   1 6 6*0 1 6 6*0 1 6 6*0 1 6 6*0 1 6 6*0 1 6 6*0 1 6 6*0 1 6 6*0 1 6 6*0 1 6 6*0 1 6 6*0 1 6 6*0 1 6
  //   6*0 1 6 10 5*0 1 6 6*0 1 6 10 5*0 1 6 6*0 1 6 6*0 1 6 6*0 1 6 40 5*0 1 6 4000 400 2000 0 0 0 1 6 6*0
  //   1 6 6*0 1 6 6*0 1 6 6*0 1 6 6*0 1 6 6*0 1 6 6*0 1 6 6*0 1 6 6*0 1 6 10 2 4*0 1 6 10 2 4*0 1 6 10 2
  //   4*0 1 6 10 2 4*0 1 6 10 2 4*0 1 6 10 5*0 1 6 10 1 4*0 1 6 10 5*0 1 6 10 5*0 1 6 10 5*0 1 6 10 2000
  //   4*0 1 6 10 80 4*0 1 6 10 20 4*0 1 6 10 40 4*0 1 6 10 200 4*0 1 6 10 2 400 0 0 0 1 6 10 2 800 0 0 0 1
  //   6 10 2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
  //   contents of rom_2 (hex, n*v repeats v):
  //   1 2 6*0 1 2 1 4 4*0 1 2 1 8 4*0 1 2 1 20 4*0 1 2 1 40 4*0 1 2 1 100 4*0 1 2 4 5*0 1 2 8 5*0 1 2 20
  //   5*0 1 2 40 5*0 1 2 100 5*0 1 2 1 400 4*0 1 2 1 400 4*0 1 2 1 400 4*0 1 2 1 400 4*0 1 2 1 400 200 0 0
  //   0 1 2 1 8 4 0 0 0 1 2 1 8 4 0 0 0 1 2 1 8 4*0 1 2 8 4 4*0 1 2 8 4 4*0 1 2 6*0 1 2 6*0 1 2 6*0 1 2
  //   6*0 1 2 6*0 1 2 6*0 1 2 6*0 1 2 6*0 1 2 6*0 1 2 6*0 1 2 6*0 1 2 1 400 4*0 1 2 1 40 4*0 1 2 100 5*0 1
  //   2 6*0 1 2 6*0 1 2 6*0 1 2 6*0 1 2 6*0 1 2 6*0 1 2 6*0 1 2 6*0 1 2 6*0 1 2 6*0 1 2 6*0 1 2 6*0 1 2
  //   6*0 1 2 0 800 2000 0 0 0 1 2 2000 800 1000 0 0 0 1 2 0 800 8 2000 0 0 1 2 6*0 1 2 6*0 1 2 6*0 1 2
  //   6*0 1 2 6*0 1 2 6*0 1 2 6*0 1 2 6*0 1 2 6*0 1 2 6*0 1 2 6*0 1 2 6*0 1 2 6*0 1 2 80 5*0 1 2 4000 5*0
  //   1 2 8000 5*0 1 2 1 80 4*0 1 2 1 4000 4*0 1 2 6*0 1 2 6*0 1 2 6*0 1 2 6*0 1 2 6*0 1 2 6*0 1 2 6*0 1 2
  //   6*0 1 2 6*0 1 2 6*0 1 2 6*0 1 2 1 400 4*0 1 2 1 8 4 0 0 0 1 2 1 8 4 0 0 0 1 2 1 8 4 0 0 0 1 2 6*0 1
  //   2 6*0 1 2 6*0 1 2 6*0 1 2 6*0 1 2 6*0 1 2 6*0 1 2 6*0 1 2 6*0 1 2 6*0 1 2 6*0 1 2 6*0 1 2 6*0 1 2
  //   6*0 1 2 6*0 1 2 6*0 1 2 6*0 1 2 6*0 1 2 6*0 1 2 6*0 1 2 6*0 1 2 6*0 1 2 6*0 1 2 6*0 1 2 6*0 1 2 6*0
  //   1 2 6*0 1 2 6*0 1 2 2000 5*0 1 2 6*0 1 2 6*0 1 2 6*0 1 2 6*0 1 2 6*0 1 2 2000 5*0 1 2 8 4 2000 0 0 0
  //   1 2 6*0 1 2 6*0 1 2 6*0 1 2 6*0 1 2 6*0 1 2 6*0 1 2 6*0 1 2 6*0 1 2 6*0 1 2 1 4 4*0 1 2 1 8 4*0 1 2
  //   1 20 4*0 1 2 1 40 4*0 1 2 1 100 4*0 1 2 4 5*0 1 2 8 5*0 1 2 20 5*0 1 2 40 5*0 1 2 100 5*0 1 2 1 400
  //   4*0 1 2 1 400 4*0 1 2 1 400 4*0 1 2 1 400 4*0 1 2 1 400 200 0 0 0 1 2 1 8 4 0 0 0 1 2 1 8 4 0 0 0 1
  //   2 1 8 4*0 1 2 8 4 4*0 1 2 8 4 4*0 1 2 6*0 1 2 6*0 1 2 6*0 1 2 6*0 1 2 6*0 1 2 6*0 1 2 6*0 1 2 6*0 1
  //   2 6*0 1 2 6*0 1 2 6*0 1 2 1 400 4*0 1 2 1 40 4*0 1 2 100 5*0 1 2 6*0 1 2 6*0 1 2 6*0 1 2 6*0 1 2 6*0
  //   1 2 6*0 1 2 6*0 1 2 6*0 1 2 6*0 1 2 6*0 1 2 6*0 1 2 6*0 1 2 6*0 1 2 0 800 2000 0 0 0 1 2 2000 800
  //   1000 0 0 0 1 2 0 800 8 2000 0 0 1 2 6*0 1 2 6*0 1 2 6*0 1 2 6*0 1 2 6*0 1 2 6*0 1 2 6*0 1 2 6*0 1 2
  //   6*0 1 2 6*0 1 2 6*0 1 2 6*0 1 2 6*0 1 2 80 5*0 1 2 4000 5*0 1 2 8000 5*0 1 2 1 80 4*0 1 2 1 4000 4*0
  //   1 2 6*0 1 2 6*0 1 2 6*0 1 2 6*0 1 2 6*0 1 2 6*0 1 2 6*0 1 2 6*0 1 2 6*0 1 2 6*0 1 2 6*0 1 2 1 400
  //   4*0 1 2 1 8 4 0 0 0 1 2 1 8 4 0 0 0 1 2 1 8 4 0 0 0 1 2 6*0 1 2 6*0 1 2 6*0 1 2 6*0 1 2 6*0 1 2 6*0
  //   1 2 6*0 1 2 6*0 1 2 6*0 1 2 6*0 1 2 6*0 1 2 6*0 1 2 6*0 1 2 6*0 1 2 6*0 1 2 6*0 1 2 6*0 1 2 6*0 1 2
  //   6*0 1 2 6*0 1 2 6*0 1 2 6*0 1 2 6*0 1 2 6*0 1 2 6*0 1 2 6*0 1 2 6*0 1 2 6*0 1 2 2000 5*0 1 2 2000 10
  //   4*0 1 2 6*0 1 2 6*0 1 2 6*0 1 2 6*0 1 2 2000 5*0 1 2 8 4 2000 0 0 0 1 2 6*0 1 2 6*0 1 2 6*0 1 2 6*0
  //   1 2 6*0 1 2 6*0 1 2 6*0 1 2 6*0 1 2 6*0 1 2 1 4 4*0 1 2 1 8 4*0 1 2 1 20 4*0 1 2 1 40 4*0 1 2 1 100
  //   4*0 1 2 4 5*0 1 2 8 5*0 1 2 20 5*0 1 2 40 5*0 1 2 100 5*0 1 2 1 400 4*0 1 2 1 400 4*0 1 2 1 400 4*0
  //   1 2 1 400 4*0 1 2 1 400 200 0 0 0 1 2 1 8 4 0 0 0 1 2 1 8 4 0 0 0 1 2 1 8 4*0 1 2 8 4 4*0 1 2 8 4
  //   4*0 1 2 6*0 1 2 6*0 1 2 6*0 1 2 6*0 1 2 6*0 1 2 6*0 1 2 6*0 1 2 6*0 1 2 6*0 1 2 6*0 1 2 6*0 1 2 1
  //   400 4*0 1 2 1 40 4*0 1 2 100 5*0 1 2 6*0 1 2 6*0 1 2 6*0 1 2 6*0 1 2 6*0 1 2 6*0 1 2 6*0 1 2 6*0 1 2
  //   6*0 1 2 6*0 1 2 6*0 1 2 6*0 1 2 6*0 1 2 0 800 2000 0 0 0 1 2 2000 800 1000 0 0 0 1 2 0 800 8 2000 0
  //   0 1 2 6*0 1 2 6*0 1 2 6*0 1 2 6*0 1 2 6*0 1 2 6*0 1 2 6*0 1 2 6*0 1 2 6*0 1 2 6*0 1 2 6*0 1 2 6*0 1
  //   2 6*0 1 2 80 5*0 1 2 4000 5*0 1 2 8000 5*0 1 2 1 80 4*0 1 2 1 4000 4*0 1 2 6*0 1 2 6*0 1 2 6*0 1 2
  //   6*0 1 2 6*0 1 2 6*0 1 2 6*0 1 2 6*0 1 2 6*0 1 2 6*0 1 2 6*0 1 2 1 400 4*0 1 2 1 8 4 0 0 0 1 2 1 8 4
  //   0 0 0 1 2 1 8 4 0 0 0 1 2 6*0 1 2 6*0 1 2 6*0 1 2 6*0 1 2 6*0 1 2 6*0 1 2 6*0 1 2 6*0 1 2 6*0 1 2
  //   6*0 1 2 6*0 1 2 6*0 1 2 6*0 1 2 6*0 1 2 6*0 1 2 6*0 1 2 6*0 1 2 6*0 1 2 6*0 1 2 6*0 1 2 6*0 1 2 6*0
  //   1 2 6*0 1 2 6*0 1 2 6*0 1 2 6*0 1 2 6*0 1 2 6*0 1 2 2000 5*0 1 2 6*0 1 2 2000 10 4*0 1 2 6*0 1 2 6*0
  //   1 2 6*0 1 2 2000 5*0 1 2 8 4 2000 0 0 0 1 2 6*0 1 2 6*0 1 2 6*0 1 2 6*0 1 2 6*0 1 2 6*0 1 2 6*0 1 2
  //   6*0 1 2 6*0 1 2 1 4 4*0 1 2 1 8 4*0 1 2 1 20 4*0 1 2 1 40 4*0 1 2 1 100 4*0 1 2 4 5*0 1 2 8 5*0 1 2
  //   20 5*0 1 2 40 5*0 1 2 100 5*0 1 2 1 400 4*0 1 2 1 400 4*0 1 2 1 400 4*0 1 2 1 400 4*0 1 2 1 400 200
  //   0 0 0 1 2 1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
  //   contents of rom_3 (hex, n*v repeats v):
  //   643*0 1 8*0 2 7*0 4 7*0 8 998*0 1 8*0 2 7*0 4 7*0 8 998*0 1 8*0 2 7*0 4 7*0 8 998*0 1 8*0 2 7*0 4
  //   7*0 8 998*0 1 8*0 2 7*0 4 7*0 8 998*0 1 8*0 2 7*0 4 7*0 8 998*0 1 8*0 2 7*0 4 7*0 8 998*0 1 8*0 2
  //   7*0 4 7*0 8 998*0 1 8*0 2 7*0 4 7*0 8 998*0 1 8*0 2 7*0 4 7*0 8 1007*0 2 7*0 4 7*0 8 1007*0 2 7*0 4
  //   7*0 8 998*0 1 8*0 2 7*0 4 7*0 8 998*0 1 8*0 2 7*0 4 7*0 8 998*0 1 8*0 2 7*0 4 7*0 8 998*0 1 8*0 2
  //   7*0 4 7*0 8 998*0 1 8*0 2 7*0 4 7*0 8 998*0 1 8*0 2 7*0 4 7*0 8 998*0 1 8*0 2 7*0 4 7*0 8 998*0 1
  //   8*0 2 7*0 4 7*0 8 998*0 1 8*0 2 7*0 4 7*0 8 998*0 1 8*0 2 7*0 4 7*0 8 998*0 1 8*0 2 7*0 4 7*0 8
  //   998*0 1 1 7*0 2 7*0 4 0 0 0 4 0 0 0 8 998*0 1 8*0 2 7*0 4 7*0 8 998*0 1 8*0 2 7*0 4 7*0 8 998*0 1
  //   8*0 2 7*0 4 7*0 8 998*0 1 8*0 2 7*0 4 7*0 8 998*0 1 8*0 2 7*0 4 7*0 8 998*0 1 8*0 2 7*0 4 7*0 8
  //   998*0 1 8*0 2 7*0 4 7*0 8 998*0 1 8*0 2 7*0 4 7*0 8
endmodule

module ALU (
  input  BORROW_IN,
  input  CARRY_IN,
  input  [15:0] A_IN,
  input  [15:0] B_IN,
  input  ADD,
  input  SUB,
  input  NOT_A,
  input  A_AND_B,
  input  A_OR_B,
  input  A_XOR_B,
  input  A_NAND_B,
  input  A_NOR_B,
  output CARRY_OUT,
  output BORROW_OUT,
  output [15:0] DATA_OUT,
  output GREATER,
  output EQUALS,
  output LESS,
  output ZERO
);

  wire and_2_out, and_3_out, and_4_out, and_5_out, and_6_out, and_7_out, and_8_out, and_9_out, and_10_out,
       and_11_out, and_12_out, and_13_out, and_14_out, and_15_out, not_2_out, not_3_out, not_4_out,
       not_5_out, not_6_out, not_7_out, not_8_out, not_9_out, not_10_out, not_11_out, not_12_out, not_13_out,
       not_14_out, not_15_out, not_16_out, not_17_out;
  wire [15:0] adder_1_out, and_1_out, nand_1_out, nor_1_out, not_1_out, or_1_out, or_2_out, subtractor_1_out,
       xor_1_out;

  Adder #(.width(16)) adder_1 (.a(A_IN), .b(B_IN), .out(adder_1_out), .cin(CARRY_IN), .cout(CARRY_OUT));
  Subtractor #(.width(16)) subtractor_1 (
    .a(A_IN), .b(B_IN), .out(subtractor_1_out), .bin(BORROW_IN), .bout(BORROW_OUT));
  Comparator #(.width(16)) comparator_1 (.a(A_IN), .b(B_IN), .gt(GREATER), .eq(EQUALS), .lt(LESS));
  assign not_1_out = ~A_IN;  // NOT_Gate not_1, 16 bits wide
  assign DATA_OUT = NOT_A ? not_1_out : 16'bz;  // Controlled_Buffer controlled_buffer_1
  assign and_1_out = A_IN & B_IN;  // AND_Gate and_1, 16 bits wide
  assign DATA_OUT = A_AND_B ? and_1_out : 16'bz;  // Controlled_Buffer controlled_buffer_2
  assign or_1_out = A_IN | B_IN;  // OR_Gate or_1, 16 bits wide
  assign DATA_OUT = A_OR_B ? or_1_out : 16'bz;  // Controlled_Buffer controlled_buffer_3
  assign xor_1_out = A_IN ^ B_IN;  // XOR_Gate xor_1, 16 bits wide
  assign DATA_OUT = A_XOR_B ? xor_1_out : 16'bz;  // Controlled_Buffer controlled_buffer_4
  assign nand_1_out = ~(A_IN & B_IN);  // NAND_Gate nand_1, 16 bits wide
  assign DATA_OUT = A_NAND_B ? nand_1_out : 16'bz;  // Controlled_Buffer controlled_buffer_5
  assign nor_1_out = ~(A_IN | B_IN);  // NOR_Gate nor_1, 16 bits wide
  assign DATA_OUT = A_NOR_B ? nor_1_out : 16'bz;  // Controlled_Buffer controlled_buffer_6
  assign DATA_OUT = ADD ? adder_1_out : 16'bz;  // Controlled_Buffer controlled_buffer_7
  assign DATA_OUT = SUB ? subtractor_1_out : 16'bz;  // Controlled_Buffer controlled_buffer_8
  assign or_2_out = DATA_OUT;  // OR_Gate or_2, 16 bits wide OR_Gate
  not not_2 (not_2_out, or_2_out[1]);
  not not_3 (not_3_out, or_2_out[2]);
  not not_4 (not_4_out, or_2_out[0]);
  and and_2 (and_2_out, not_4_out, not_2_out);
  and and_3 (and_3_out, and_2_out, not_3_out);
  and and_4 (and_4_out, and_3_out, not_5_out);
  not not_5 (not_5_out, or_2_out[3]);
  not not_6 (not_6_out, or_2_out[4]);
  not not_7 (not_7_out, or_2_out[5]);
  not not_8 (not_8_out, or_2_out[6]);
  and and_5 (and_5_out, and_4_out, not_6_out);
  and and_6 (and_6_out, and_5_out, not_7_out);
  and and_7 (and_7_out, and_6_out, not_8_out);
  and and_8 (and_8_out, and_7_out, not_9_out);
  not not_9 (not_9_out, or_2_out[7]);
  not not_10 (not_10_out, or_2_out[8]);
  not not_11 (not_11_out, or_2_out[9]);
  not not_12 (not_12_out, or_2_out[10]);
  and and_9 (and_9_out, and_8_out, not_10_out);
  and and_10 (and_10_out, and_9_out, not_11_out);
  and and_11 (and_11_out, and_10_out, not_12_out);
  and and_12 (and_12_out, and_11_out, not_13_out);
  not not_13 (not_13_out, or_2_out[11]);
  not not_14 (not_14_out, or_2_out[12]);
  not not_15 (not_15_out, or_2_out[13]);
  not not_16 (not_16_out, or_2_out[14]);
  and and_13 (and_13_out, and_12_out, not_14_out);
  and and_14 (and_14_out, and_13_out, not_15_out);
  and and_15 (and_15_out, and_14_out, not_16_out);
  and and_16 (ZERO, and_15_out, not_17_out);
  Pull_Resistor pull_resistor_1 (.node(or_2_out[0]));
  Pull_Resistor pull_resistor_2 (.node(or_2_out[1]));
  Pull_Resistor pull_resistor_3 (.node(or_2_out[2]));
  Pull_Resistor pull_resistor_4 (.node(or_2_out[3]));
  Pull_Resistor pull_resistor_5 (.node(or_2_out[4]));
  Pull_Resistor pull_resistor_6 (.node(or_2_out[5]));
  Pull_Resistor pull_resistor_7 (.node(or_2_out[6]));
  Pull_Resistor pull_resistor_8 (.node(or_2_out[7]));
  Pull_Resistor pull_resistor_9 (.node(or_2_out[8]));
  Pull_Resistor pull_resistor_10 (.node(or_2_out[9]));
  Pull_Resistor pull_resistor_11 (.node(or_2_out[10]));
  Pull_Resistor pull_resistor_12 (.node(or_2_out[11]));
  Pull_Resistor pull_resistor_13 (.node(or_2_out[12]));
  Pull_Resistor pull_resistor_14 (.node(or_2_out[13]));
  Pull_Resistor pull_resistor_15 (.node(or_2_out[14]));
  Pull_Resistor pull_resistor_16 (.node(or_2_out[15]));
  not not_17 (not_17_out, or_2_out[15]);
endmodule

module ACCULUMATOR (
  input  [15:0] DATA_IN,
  input  A_WRITE,
  input  A_READ,
  input  CLOCK,
  input  RESET,
  output [15:0] ALWAYS_OUT,
  output [15:0] DATA_OUT
);

  Register #(.width(16)) register_1 (.D(DATA_IN), .en(A_WRITE), .clk(CLOCK), .Q(ALWAYS_OUT), .clr(RESET));
  assign DATA_OUT = A_READ ? ALWAYS_OUT : 16'bz;  // Controlled_Buffer controlled_buffer_1
endmodule

module OUTPUT_REGISTER (
  input  [15:0] DATA_IN,
  input  OUTPUT_WRITE,
  input  OUTPUT_READ,
  input  CLOCK,
  input  RESET,
  output [15:0] ALWAYS_OUT,
  output [15:0] DATA_OUT
);

  Register #(.width(16)) register_1 (.D(DATA_IN), .en(OUTPUT_WRITE), .clk(CLOCK), .Q(ALWAYS_OUT), .clr(RESET));
  assign DATA_OUT = OUTPUT_READ ? ALWAYS_OUT : 16'bz;  // Controlled_Buffer controlled_buffer_1
endmodule

module PROGRAM_COUNTER (
  input  RESET,
  input  JUMP,
  input  COUNTER_ENABLE,
  input  CLOCK,
  input  [15:0] ADDRESS_IN,
  input  COUNTER_OUT,
  output [15:0] ALWAYS_OUT,
  output [15:0] ADDRESS_OUT
);

  Counter #(.max('hffff), .width(16)) counter_1 (
    .clr(RESET), .load(JUMP), .up(COUNTER_ENABLE), .count(COUNTER_ENABLE), .clk(CLOCK), .D(ADDRESS_IN),
    .Q(ALWAYS_OUT));  // open: carry
  assign ADDRESS_OUT = COUNTER_OUT ? ALWAYS_OUT : 16'bz;  // Controlled_Buffer controlled_buffer_1
endmodule

module CLK (
  input  CLOCK_IN,
  input  CLOCK_ENABLE,
  input  MANUAL_TICK,
  input  HALT,
  output CLOCK_OUT
);

  wire and_1_out, and_2_out, not_1_out, not_2_out, or_1_out;

  not not_1 (not_1_out, HALT);
  not not_2 (not_2_out, CLOCK_ENABLE);
  and and_1 (and_1_out, CLOCK_IN, CLOCK_ENABLE);
  and and_2 (and_2_out, not_2_out, MANUAL_TICK);
  or or_1 (or_1_out, and_1_out, and_2_out);
  and and_3 (CLOCK_OUT, or_1_out, not_1_out);
endmodule

module Y_AND_Y_REGISTERS (
  input  [15:0] in_1,
  input  WRITE_X,
  input  WRITE_Y,
  input  READ_X,
  input  READ_Y,
  input  CLOCK,
  input  RESET,
  output [15:0] X_ALWAYS_OUT,
  output [15:0] DATA_OUT,
  output [15:0] Y_ALWAYS_OUT
);

  Register #(.width(16)) X (.D(in_1), .en(WRITE_X), .clk(CLOCK), .Q(X_ALWAYS_OUT), .clr(RESET));
  Register #(.width(16)) Y (.D(in_1), .en(WRITE_Y), .clk(CLOCK), .Q(Y_ALWAYS_OUT), .clr(RESET));
  assign DATA_OUT = READ_X ? X_ALWAYS_OUT : 16'bz;  // Controlled_Buffer controlled_buffer_1
  assign DATA_OUT = READ_Y ? Y_ALWAYS_OUT : 16'bz;  // Controlled_Buffer controlled_buffer_2
endmodule

module FLAGS (
  input  CARRY,
  input  BORROW,
  input  GREATER,
  input  EQUALS,
  input  LESS,
  input  ZERO,
  input  ALU_FLAGS_SET,
  input  COMPARE_FALGS_SET,
  input  CLOCK,
  input  RESET,
  output CARRY_FLAG,
  output BORROW_FLAG,
  output GREATER_FLAG,
  output EQUALS_FLAG,
  output LESS_FLAG,
  output ZERO_FLAG
);

  Register #(.width(1)) register_1 (.D(CARRY), .en(ALU_FLAGS_SET), .clk(CLOCK), .Q(CARRY_FLAG), .clr(RESET));
  Register #(.width(1)) register_2 (.D(BORROW), .en(ALU_FLAGS_SET), .clk(CLOCK), .Q(BORROW_FLAG), .clr(RESET));
  Register #(.width(1)) register_3 (.D(GREATER), .en(COMPARE_FALGS_SET), .clk(CLOCK), .Q(GREATER_FLAG), .clr(RESET));
  Register #(.width(1)) register_4 (.D(EQUALS), .en(COMPARE_FALGS_SET), .clk(CLOCK), .Q(EQUALS_FLAG), .clr(RESET));
  Register #(.width(1)) register_5 (.D(LESS), .en(COMPARE_FALGS_SET), .clk(CLOCK), .Q(LESS_FLAG), .clr(RESET));
  Register #(.width(1)) register_6 (.D(ZERO), .en(ALU_FLAGS_SET), .clk(CLOCK), .Q(ZERO_FLAG), .clr(RESET));
endmodule

module B_REGISTER (
  input  [15:0] DATA_IN,
  input  B_WRITE,
  input  B_READ,
  input  CLOCK,
  input  RESET,
  output [15:0] ALWAYS_OUT,
  output [15:0] DATA_OUT
);

  Register #(.width(16)) register_1 (.D(DATA_IN), .en(B_WRITE), .clk(CLOCK), .Q(ALWAYS_OUT), .clr(RESET));
  assign DATA_OUT = B_READ ? ALWAYS_OUT : 16'bz;  // Controlled_Buffer controlled_buffer_1
endmodule

module MEMORY_ADDRESS_REGISTER (
  input  [15:0] DATA_IN,
  input  MAR_IN,
  input  MAR_OUT,
  input  CLOCK,
  input  MAR_RESET,
  output [15:0] ALWAYS_OUT,
  output [15:0] DATA_OUT
);

  Register #(.width(16)) register_1 (.D(DATA_IN), .en(MAR_IN), .clk(CLOCK), .Q(ALWAYS_OUT), .clr(MAR_RESET));
  assign DATA_OUT = MAR_OUT ? ALWAYS_OUT : 16'bz;  // Controlled_Buffer controlled_buffer_1
endmodule

module INSTRUCTION_REGISTER (
  input  [15:0] DATA_IN,
  input  STORE,
  input  DATA_OUT_ENABLE,
  input  RESET,
  input  CLOCK,
  output [15:0] ALWAYS_OUT,
  output [15:0] DATA_OUT
);

  Register #(.width(16)) register_1 (.D(DATA_IN), .en(STORE), .clk(CLOCK), .Q(ALWAYS_OUT), .clr(RESET));
  assign DATA_OUT = DATA_OUT_ENABLE ? ALWAYS_OUT : 16'bz;  // Controlled_Buffer controlled_buffer_1
endmodule

module STEP_COUNTER (
  input  RESET,
  input  CLOCK,
  output [3:0] BINARY_OUT
);

  Counter #(.max('hf), .width(4)) counter_1 (
    .clr(RESET), .up(1'b1), .count(1'b1), .clk(CLOCK), .Q(BINARY_OUT));  // open: load, D, carry
endmodule

module FRAME_BUFFER (
  input  Clock,
  input  DATA,
  input  WRITE_ENB,
  input  RESET,
  input  X_CORD_0,
  input  X_CORD_1,
  input  Y_CORD_0,
  input  Y_CORD_1,
  output [3:0] ONE,
  output [3:0] TWO,
  output [3:0] THREE,
  output [3:0] ZERO
);

  wire demultiplexer_1_out0, demultiplexer_1_out1, demultiplexer_1_out2, demultiplexer_1_out3,
       demultiplexer_2_out0, demultiplexer_2_out1, demultiplexer_2_out2, demultiplexer_2_out3,
       demultiplexer_4_out0, demultiplexer_4_out1, demultiplexer_4_out2, demultiplexer_4_out3,
       demultiplexer_5_out0, demultiplexer_5_out1, demultiplexer_5_out2, demultiplexer_5_out3,
       demultiplexer_6_out0, demultiplexer_6_out1, demultiplexer_6_out2, demultiplexer_6_out3,
       demultiplexer_7_out0, demultiplexer_7_out1, demultiplexer_7_out2, demultiplexer_7_out3,
       demultiplexer_8_out0, demultiplexer_8_out1, demultiplexer_8_out2, demultiplexer_8_out3,
       demultiplexer_9_out0, demultiplexer_9_out1, demultiplexer_9_out2, demultiplexer_9_out3,
       demultiplexer_10_out0, demultiplexer_10_out1, demultiplexer_10_out2, demultiplexer_10_out3,
       demultiplexer_11_out0, demultiplexer_11_out1, demultiplexer_11_out2, demultiplexer_11_out3,
       demultiplexer_12_out0, demultiplexer_12_out1, demultiplexer_12_out2, demultiplexer_12_out3,
       demultiplexer_13_out0, demultiplexer_13_out1, demultiplexer_13_out2, demultiplexer_13_out3,
       demultiplexer_14_out0, demultiplexer_14_out1, demultiplexer_14_out2, demultiplexer_14_out3,
       pull_resistor_1_node;
  wire [1:0] demultiplexer_3_out0, demultiplexer_3_out1, demultiplexer_3_out2, demultiplexer_3_out3;

  Demultiplexer #(.enable("true"), .select(2)) demultiplexer_1 (
    .out0(demultiplexer_1_out0), .out1(demultiplexer_1_out1), .out2(demultiplexer_1_out2),
    .out3(demultiplexer_1_out3), .in(RESET), .sel(demultiplexer_3_out0), .en(demultiplexer_4_out0));
  Demultiplexer #(.enable("true"), .select(2)) demultiplexer_2 (
    .out0(demultiplexer_2_out0), .out1(demultiplexer_2_out1), .out2(demultiplexer_2_out2),
    .out3(demultiplexer_2_out3), .in(DATA), .sel(demultiplexer_3_out0), .en(demultiplexer_4_out0));
  Demultiplexer #(.select(2), .width(2)) demultiplexer_3 (
    .out0(demultiplexer_3_out0), .out1(demultiplexer_3_out1), .out2(demultiplexer_3_out2),
    .out3(demultiplexer_3_out3), .in({Y_CORD_1, Y_CORD_0}), .sel({X_CORD_1, X_CORD_0}));
  Pull_Resistor #(.pull(1)) pull_resistor_1 (.node(pull_resistor_1_node));
  Demultiplexer #(.select(2)) demultiplexer_4 (
    .out0(demultiplexer_4_out0), .out1(demultiplexer_4_out1), .out2(demultiplexer_4_out2),
    .out3(demultiplexer_4_out3), .in(pull_resistor_1_node), .sel({X_CORD_1, X_CORD_0}));
  Demultiplexer #(.enable("true"), .select(2)) demultiplexer_5 (
    .out0(demultiplexer_5_out0), .out1(demultiplexer_5_out1), .out2(demultiplexer_5_out2),
    .out3(demultiplexer_5_out3), .in(DATA), .sel(demultiplexer_3_out1), .en(demultiplexer_4_out1));
  Demultiplexer #(.enable("true"), .select(2)) demultiplexer_6 (
    .out0(demultiplexer_6_out0), .out1(demultiplexer_6_out1), .out2(demultiplexer_6_out2),
    .out3(demultiplexer_6_out3), .in(DATA), .sel(demultiplexer_3_out2), .en(demultiplexer_4_out2));
  Demultiplexer #(.enable("true"), .select(2)) demultiplexer_7 (
    .out0(demultiplexer_7_out0), .out1(demultiplexer_7_out1), .out2(demultiplexer_7_out2),
    .out3(demultiplexer_7_out3), .in(DATA), .sel(demultiplexer_3_out3), .en(demultiplexer_4_out3));
  Register #(.width(1)) register_1 (
    .D(demultiplexer_2_out0), .en(demultiplexer_8_out0), .clk(Clock), .Q(ZERO[3]), .clr(demultiplexer_1_out0));
  Register #(.width(1)) register_2 (
    .D(demultiplexer_2_out1), .en(demultiplexer_8_out1), .clk(Clock), .Q(ZERO[2]), .clr(demultiplexer_1_out1));
  Register #(.width(1)) register_3 (
    .D(demultiplexer_2_out2), .en(demultiplexer_8_out2), .clk(Clock), .Q(ZERO[1]), .clr(demultiplexer_1_out2));
  Register #(.width(1)) register_4 (
    .D(demultiplexer_2_out3), .en(demultiplexer_8_out3), .clk(Clock), .Q(ZERO[0]), .clr(demultiplexer_1_out3));
  Demultiplexer #(.enable("true"), .select(2)) demultiplexer_8 (
    .out0(demultiplexer_8_out0), .out1(demultiplexer_8_out1), .out2(demultiplexer_8_out2),
    .out3(demultiplexer_8_out3), .in(WRITE_ENB), .sel(demultiplexer_3_out0), .en(demultiplexer_4_out0));
  Demultiplexer #(.enable("true"), .select(2)) demultiplexer_9 (
    .out0(demultiplexer_9_out0), .out1(demultiplexer_9_out1), .out2(demultiplexer_9_out2),
    .out3(demultiplexer_9_out3), .in(RESET), .sel(demultiplexer_3_out1), .en(demultiplexer_4_out1));
  Register #(.width(1)) register_5 (
    .D(demultiplexer_5_out0), .en(demultiplexer_10_out0), .clk(Clock), .Q(ONE[3]), .clr(demultiplexer_9_out0));
  Register #(.width(1)) register_6 (
    .D(demultiplexer_5_out1), .en(demultiplexer_10_out1), .clk(Clock), .Q(ONE[2]), .clr(demultiplexer_9_out1));
  Register #(.width(1)) register_7 (
    .D(demultiplexer_5_out2), .en(demultiplexer_10_out2), .clk(Clock), .Q(ONE[1]), .clr(demultiplexer_9_out2));
  Register #(.width(1)) register_8 (
    .D(demultiplexer_5_out3), .en(demultiplexer_10_out3), .clk(Clock), .Q(ONE[0]), .clr(demultiplexer_9_out3));
  Demultiplexer #(.enable("true"), .select(2)) demultiplexer_10 (
    .out0(demultiplexer_10_out0), .out1(demultiplexer_10_out1), .out2(demultiplexer_10_out2),
    .out3(demultiplexer_10_out3), .in(WRITE_ENB), .sel(demultiplexer_3_out1), .en(demultiplexer_4_out1));
  Demultiplexer #(.enable("true"), .select(2)) demultiplexer_11 (
    .out0(demultiplexer_11_out0), .out1(demultiplexer_11_out1), .out2(demultiplexer_11_out2),
    .out3(demultiplexer_11_out3), .in(RESET), .sel(demultiplexer_3_out2), .en(demultiplexer_4_out2));
  Register #(.width(1)) register_9 (
    .D(demultiplexer_6_out0), .en(demultiplexer_12_out0), .clk(Clock), .Q(TWO[3]), .clr(demultiplexer_11_out0));
  Register #(.width(1)) register_10 (
    .D(demultiplexer_6_out1), .en(demultiplexer_12_out1), .clk(Clock), .Q(TWO[2]), .clr(demultiplexer_11_out1));
  Register #(.width(1)) register_11 (
    .D(demultiplexer_6_out2), .en(demultiplexer_12_out2), .clk(Clock), .Q(TWO[1]), .clr(demultiplexer_11_out2));
  Register #(.width(1)) register_12 (
    .D(demultiplexer_6_out3), .en(demultiplexer_12_out3), .clk(Clock), .Q(TWO[0]), .clr(demultiplexer_11_out3));
  Demultiplexer #(.enable("true"), .select(2)) demultiplexer_12 (
    .out0(demultiplexer_12_out0), .out1(demultiplexer_12_out1), .out2(demultiplexer_12_out2),
    .out3(demultiplexer_12_out3), .in(WRITE_ENB), .sel(demultiplexer_3_out2), .en(demultiplexer_4_out2));
  Demultiplexer #(.enable("true"), .select(2)) demultiplexer_13 (
    .out0(demultiplexer_13_out0), .out1(demultiplexer_13_out1), .out2(demultiplexer_13_out2),
    .out3(demultiplexer_13_out3), .in(RESET), .sel(demultiplexer_3_out3), .en(demultiplexer_4_out3));
  Register #(.width(1)) register_13 (
    .D(demultiplexer_7_out0), .en(demultiplexer_14_out0), .clk(Clock), .Q(THREE[3]),
    .clr(demultiplexer_13_out0));
  Register #(.width(1)) register_14 (
    .D(demultiplexer_7_out1), .en(demultiplexer_14_out1), .clk(Clock), .Q(THREE[2]),
    .clr(demultiplexer_13_out1));
  Register #(.width(1)) register_15 (
    .D(demultiplexer_7_out2), .en(demultiplexer_14_out2), .clk(Clock), .Q(THREE[1]),
    .clr(demultiplexer_13_out2));
  Register #(.width(1)) register_16 (
    .D(demultiplexer_7_out3), .en(demultiplexer_14_out3), .clk(Clock), .Q(THREE[0]),
    .clr(demultiplexer_13_out3));
  Demultiplexer #(.enable("true"), .select(2)) demultiplexer_14 (
    .out0(demultiplexer_14_out0), .out1(demultiplexer_14_out1), .out2(demultiplexer_14_out2),
    .out3(demultiplexer_14_out3), .in(WRITE_ENB), .sel(demultiplexer_3_out3), .en(demultiplexer_4_out3));
endmodule

module video_buffer (
  input  [7:0] DATA_IN,
  input  DATA_WRITE_ENABLE,
  input  [2:0] ADDRESS_SELECT,
  input  BUFFER_ADDRESS_WRITE_ENB,
  input  CLOCK,
  input  RESET_BUFFER,
  input  UPDATE_DISPLAY,
  input  RESET_DISPLAY,
  output [7:0] LINE_1,
  output [7:0] LINE_2,
  output [7:0] LINE_3,
  output [7:0] LINE_4,
  output [7:0] LINE_5,
  output [7:0] LINE_6,
  output [7:0] LINE_7,
  output [7:0] LINE_8
);

  wire demultiplexer_1_out0, demultiplexer_1_out1, demultiplexer_1_out2, demultiplexer_1_out3,
       demultiplexer_1_out4, demultiplexer_1_out5, demultiplexer_1_out6, demultiplexer_1_out7;
  wire [2:0] register_1_q;
  wire [7:0] register_2_q, register_3_q, register_4_q, register_5_q, register_6_q, register_7_q,
       register_8_q, register_9_q;

  Register #(.width(3)) register_1 (
    .D(ADDRESS_SELECT), .en(BUFFER_ADDRESS_WRITE_ENB), .clk(CLOCK), .Q(register_1_q));  // open: clr
  Demultiplexer #(.select(3)) demultiplexer_1 (
    .out0(demultiplexer_1_out0), .out1(demultiplexer_1_out1), .out2(demultiplexer_1_out2),
    .out3(demultiplexer_1_out3), .out4(demultiplexer_1_out4), .out5(demultiplexer_1_out5),
    .out6(demultiplexer_1_out6), .out7(demultiplexer_1_out7), .in(DATA_WRITE_ENABLE), .sel(register_1_q));
  Register register_2 (.D(DATA_IN), .en(demultiplexer_1_out0), .clk(CLOCK), .Q(register_2_q), .clr(RESET_BUFFER));
  Register register_3 (.D(DATA_IN), .en(demultiplexer_1_out1), .clk(CLOCK), .Q(register_3_q), .clr(RESET_BUFFER));
  Register register_4 (.D(DATA_IN), .en(demultiplexer_1_out2), .clk(CLOCK), .Q(register_4_q), .clr(RESET_BUFFER));
  Register register_5 (.D(DATA_IN), .en(demultiplexer_1_out3), .clk(CLOCK), .Q(register_5_q), .clr(RESET_BUFFER));
  Register register_6 (.D(DATA_IN), .en(demultiplexer_1_out4), .clk(CLOCK), .Q(register_6_q), .clr(RESET_BUFFER));
  Register register_7 (.D(DATA_IN), .en(demultiplexer_1_out5), .clk(CLOCK), .Q(register_7_q), .clr(RESET_BUFFER));
  Register register_8 (.D(DATA_IN), .en(demultiplexer_1_out6), .clk(CLOCK), .Q(register_8_q), .clr(RESET_BUFFER));
  Register register_9 (.D(DATA_IN), .en(demultiplexer_1_out7), .clk(CLOCK), .Q(register_9_q), .clr(RESET_BUFFER));
  Register register_10 (.D(register_2_q), .en(UPDATE_DISPLAY), .clk(CLOCK), .Q(LINE_1), .clr(RESET_DISPLAY));
  Register register_11 (.D(register_3_q), .en(UPDATE_DISPLAY), .clk(CLOCK), .Q(LINE_2), .clr(RESET_DISPLAY));
  Register register_12 (.D(register_4_q), .en(UPDATE_DISPLAY), .clk(CLOCK), .Q(LINE_3), .clr(RESET_DISPLAY));
  Register register_13 (.D(register_5_q), .en(UPDATE_DISPLAY), .clk(CLOCK), .Q(LINE_4), .clr(RESET_DISPLAY));
  Register register_14 (.D(register_6_q), .en(UPDATE_DISPLAY), .clk(CLOCK), .Q(LINE_5), .clr(RESET_DISPLAY));
  Register register_15 (.D(register_7_q), .en(UPDATE_DISPLAY), .clk(CLOCK), .Q(LINE_6), .clr(RESET_DISPLAY));
  Register register_16 (.D(register_8_q), .en(UPDATE_DISPLAY), .clk(CLOCK), .Q(LINE_7), .clr(RESET_DISPLAY));
  Register register_17 (.D(register_9_q), .en(UPDATE_DISPLAY), .clk(CLOCK), .Q(LINE_8), .clr(RESET_DISPLAY));
endmodule

module DISPLAY (
  input  in_1,
  input  [2:0] in_2,
  input  [7:0] in_3,
  input  in_4,
  input  in_5,
  input  in_6
);

  wire [7:0] video_buffer_1_line_1, video_buffer_1_line_2, video_buffer_1_line_3, video_buffer_1_line_4,
       video_buffer_1_line_5, video_buffer_1_line_6, video_buffer_1_line_7, video_buffer_1_line_8;

  DotMatrix #(.inputtype("row"), .matrixcols(8), .matrixrows(8)) dotmatrix_1 (
    .row0(video_buffer_1_line_1), .row1(video_buffer_1_line_2), .row2(video_buffer_1_line_3),
    .row3(video_buffer_1_line_4), .row4(video_buffer_1_line_5), .row5(video_buffer_1_line_6),
    .row6(video_buffer_1_line_7), .row7(video_buffer_1_line_8));
  video_buffer video_buffer_1 (
    .DATA_WRITE_ENABLE(in_6), .CLOCK(in_1), .UPDATE_DISPLAY(in_4), .DATA_IN(in_3), .ADDRESS_SELECT(in_2),
    .BUFFER_ADDRESS_WRITE_ENB(in_5), .LINE_1(video_buffer_1_line_1), .LINE_2(video_buffer_1_line_2),
    .LINE_3(video_buffer_1_line_3), .LINE_4(video_buffer_1_line_4), .LINE_5(video_buffer_1_line_5),
    .LINE_6(video_buffer_1_line_6), .LINE_7(video_buffer_1_line_7), .LINE_8(video_buffer_1_line_8));  // open: RESET_DISPLAY, RESET_BUFFER
endmodule
